// Digital circuit Flip Flop tipo D.dig as structural Verilog
module Flip_Flop_tipo_D (
  input  D,
  input  clk,
  output Q,
  output Q_2
);

  wire nand_1_out, nand_2_out, not_1_out;

  not not_1 (not_1_out, D);
  nand nand_1 (nand_1_out, D, Q_2, clk);
  nand nand_2 (nand_2_out, clk, not_1_out, Q);
  nand nand_3 (Q, nand_1_out, Q_2);
  nand nand_4 (Q_2, Q, nand_2_out);
endmodule
