// Digital circuit ULAprincipal.dig as structural Verilog
module ULAprincipal (
  input  nINV,
  input  CY,
  input  [7:0] A,
  input  [7:0] B,
  input  SUB,
  output C_out,
  output Flg_Z,
  output Flg_Neg,
  output [7:0] O
);

  wire or_1_out, sapula0_1_p7, sapula0_2_p7, sapula0_3_p7, sapula0_4_p7, sapula0_5_p7, sapula0_6_p7,
       sapula0_7_p7, xor_1_out;

  or or_1 (or_1_out, CY, SUB);
  // sapULA0 sapula0_1: pin names not known; wires that end beside it: or_1_out, A[0], B[0], SUB, nINV, O[0], sapula0_1_p7
  // sapULA0 sapula0_2: pin names not known; wires that end beside it: sapula0_1_p7, A[1], B[1], SUB, nINV, O[1], sapula0_2_p7
  // sapULA0 sapula0_3: pin names not known; wires that end beside it: sapula0_2_p7, A[2], B[2], SUB, nINV, O[2], sapula0_3_p7
  // sapULA0 sapula0_4: pin names not known; wires that end beside it: sapula0_3_p7, A[3], B[3], SUB, nINV, O[3], sapula0_4_p7
  // sapULA0 sapula0_5: pin names not known; wires that end beside it: sapula0_4_p7, A[4], B[4], SUB, nINV, O[4], sapula0_5_p7
  // sapULA0 sapula0_6: pin names not known; wires that end beside it: sapula0_5_p7, A[5], B[5], SUB, nINV, O[5], sapula0_6_p7
  // sapULA0 sapula0_7: pin names not known; wires that end beside it: sapula0_6_p7, A[6], B[6], SUB, nINV, O[6], sapula0_7_p7
  // sapULA0 sapula0_8: pin names not known; wires that end beside it: sapula0_7_p7, A[7], B[7], SUB, nINV, O[7], C_out
  xor xor_1 (xor_1_out, SUB, C_out);
  Seven_Seg_Hex seven_seg_hex_1 (.d(A[7:4]), .dp(1'b0));
  Seven_Seg_Hex seven_seg_hex_2 (.d(O[7:4]), .dp(1'b0));
  Seven_Seg_Hex seven_seg_hex_3 (.d(A[3:0]), .dp(1'b0));
  Seven_Seg_Hex seven_seg_hex_4 (.d(O[3:0]), .dp(1'b0));
  nor nor_1 (Flg_Z, O[0], O[1], O[2], O[3], O[4], O[5], O[6], O[7]);
  and and_1 (Flg_Neg, SUB, xor_1_out);
  Seven_Seg_Hex seven_seg_hex_5 (.d(B[7:4]), .dp(1'b0));
  Seven_Seg_Hex seven_seg_hex_6 (.d(B[3:0]), .dp(1'b0));

  // Other names for the same wires on the sheet: RA[7:0] = A; RB[7:0] = B

  // Notes on the sheet:
  //   nINV: default 1
endmodule
