// Digital circuit regis8bits.dig as structural Verilog
module regis8bits (
  input  D3,
  input  ENA_i,
  input  D2,
  input  D1,
  input  D0,
  input  D7,
  input  D6,
  input  D5,
  input  D4,
  input  ENA_o,
  output Q3,
  output Q2,
  output Q1,
  output Q0,
  output Q7,
  output Q6,
  output Q5,
  output Q4
);

  wire nand_1_out, nand_2_out, nand_3_out, nand_4_out, nand_5_out, nand_6_out, nand_7_out, nand_8_out,
       nand_9_out, nand_10_out, nand_11_out, nand_12_out, nand_13_out, nand_14_out, nand_15_out, nand_16_out,
       nand_17_out, nand_18_out, nand_19_out, nand_20_out, nand_21_out, nand_22_out, nand_23_out,
       nand_24_out, nand_25_out, nand_26_out, nand_27_out, nand_28_out, nand_29_out, nand_30_out,
       nand_31_out, nand_32_out, not_1_out, not_2_out, not_3_out, not_4_out, not_5_out, not_6_out, not_7_out,
       not_8_out;

  not not_1 (not_1_out, D0);
  not not_2 (not_2_out, D1);
  not not_3 (not_3_out, D2);
  not not_4 (not_4_out, D3);
  nand nand_1 (nand_1_out, D0, ENA_i);
  nand nand_2 (nand_2_out, not_1_out, ENA_i);
  nand nand_3 (nand_3_out, D1, ENA_i);
  nand nand_4 (nand_4_out, not_2_out, ENA_i);
  nand nand_5 (nand_5_out, D2, ENA_i);
  nand nand_6 (nand_6_out, not_3_out, ENA_i);
  nand nand_7 (nand_7_out, D3, ENA_i);
  nand nand_8 (nand_8_out, not_4_out, ENA_i);
  nand nand_9 (nand_9_out, nand_1_out, nand_10_out);
  nand nand_10 (nand_10_out, nand_9_out, nand_2_out);
  nand nand_11 (nand_11_out, nand_3_out, nand_12_out);
  nand nand_12 (nand_12_out, nand_11_out, nand_4_out);
  nand nand_13 (nand_13_out, nand_5_out, nand_14_out);
  nand nand_14 (nand_14_out, nand_13_out, nand_6_out);
  nand nand_15 (nand_15_out, nand_7_out, nand_16_out);
  nand nand_16 (nand_16_out, nand_15_out, nand_8_out);
  assign Q0 = ENA_o ? nand_9_out : 1'bz;  // Driver driver_1
  assign Q1 = ENA_o ? nand_11_out : 1'bz;  // Driver driver_2
  assign Q2 = ENA_o ? nand_13_out : 1'bz;  // Driver driver_3
  assign Q3 = ENA_o ? nand_15_out : 1'bz;  // Driver driver_4
  not not_5 (not_5_out, D4);
  not not_6 (not_6_out, D5);
  not not_7 (not_7_out, D6);
  not not_8 (not_8_out, D7);
  nand nand_17 (nand_17_out, D4, ENA_i);
  nand nand_18 (nand_18_out, not_5_out, ENA_i);
  nand nand_19 (nand_19_out, D5, ENA_i);
  nand nand_20 (nand_20_out, not_6_out, ENA_i);
  nand nand_21 (nand_21_out, D6, ENA_i);
  nand nand_22 (nand_22_out, not_7_out, ENA_i);
  nand nand_23 (nand_23_out, D7, ENA_i);
  nand nand_24 (nand_24_out, not_8_out, ENA_i);
  nand nand_25 (nand_25_out, nand_17_out, nand_26_out);
  nand nand_26 (nand_26_out, nand_25_out, nand_18_out);
  nand nand_27 (nand_27_out, nand_19_out, nand_28_out);
  nand nand_28 (nand_28_out, nand_27_out, nand_20_out);
  nand nand_29 (nand_29_out, nand_21_out, nand_30_out);
  nand nand_30 (nand_30_out, nand_29_out, nand_22_out);
  nand nand_31 (nand_31_out, nand_23_out, nand_32_out);
  nand nand_32 (nand_32_out, nand_31_out, nand_24_out);
  assign Q4 = ENA_o ? nand_25_out : 1'bz;  // Driver driver_5
  assign Q5 = ENA_o ? nand_27_out : 1'bz;  // Driver driver_6
  assign Q6 = ENA_o ? nand_29_out : 1'bz;  // Driver driver_7
  assign Q7 = ENA_o ? nand_31_out : 1'bz;  // Driver driver_8
endmodule
