// Digital circuit sapULA0.dig as structural Verilog
module sapULA0 (
  input  Carry_in,
  input  A,
  input  nInverter,
  input  B,
  input  SUB,
  output S,
  output Carry_ou
);

  wire and_1_out, and_2_out, and_3_out, and_4_out, not_1_out, xor_1_out, xor_2_out;

  xor xor_1 (xor_1_out, B, SUB);
  and and_1 (and_1_out, Carry_in, nInverter);
  not not_1 (not_1_out, nInverter);
  and and_2 (and_2_out, nInverter, xor_1_out);
  xor xor_2 (xor_2_out, A, not_1_out, and_2_out);
  and and_3 (and_3_out, A, and_2_out);
  xor xor_3 (S, and_1_out, xor_2_out);
  and and_4 (and_4_out, and_1_out, xor_2_out);
  or or_1 (Carry_ou, and_4_out, and_3_out);
endmodule
